# Fritzing sketch NodeMCU-LED Strip Fritzing Sketch (saved by Fritzing 0.9.3b)

parts:
  Gizwits_WiFi_Witty_ESP-12F1 = Gizwits WiFi Witty ESP-12F
  Relay = G3VM-61E1 [package=g3vm-61e1]
  D1 = LTE-302 [package=lte-302]
  VCC1 = Battery block 9V  # not connected

nets:
  N1: Gizwits_WiFi_Witty_ESP-12F1.VCC, Relay.P$2
  N2: Gizwits_WiFi_Witty_ESP-12F1.GND, Relay.P$3
  N3: Gizwits_WiFi_Witty_ESP-12F1.GPIO4, Relay.P$1
  N4: Relay.P$5, D1.A

notes:
  **board is different
  Node MCU plug in with USB
  Use Silicon Labs
  CP210x_Universal_Windows_Driver
  usb-to-uart-bridge
  Using Digital pin 07 on Node MCU
  Positive wire from power is connected to relay and then to LED Strip
  NegativePower to LED strip.
